# Fritzing sketch Fritzing (saved by Fritzing 0.9.1b)
breadboards: 1

parts:
  Circuit = Arduino Uno (Rev3)
  LED1 = LEDs [package=led10mm]
  LED2 = LEDs [package=led10mm]
  R1 = Resistor [tolerance=±5% resistance=330 package="0805 [SMD]"]
  R2 = Resistor [tolerance=±5% resistance=330 package="0805 [SMD]"]
  S1 = Pushbutton [package="[SMD]"]
  S2 = Pushbutton [package="[SMD]"]
  R3 = Resistor [tolerance=±5% resistance=10k package="0805 [SMD]"]
  R4 = Resistor [tolerance=±5% resistance=10k package="0805 [SMD]"]
  Potentiometer = POT [package=pot_mammoth]
  Touch_Sensor_(Linear_Pot) = POT [package=pot_mammoth]

nets:
  N1: Circuit.A0, Potentiometer.A
  N2: Circuit.A1, Touch_Sensor_(Linear_Pot).A
  N3: Circuit.GND, R1.Pin_0, R2.Pin_0, R3.Pin_0, R4.Pin_0, Potentiometer.E, Touch_Sensor_(Linear_Pot).E
  N4: Circuit.D2, S2.Pin_1, S2.Pin_2, R4.Pin_1
  N5: Circuit.D3_PWM, S1.Pin_1, S1.Pin_2, R3.Pin_1
  N6: Circuit.D6_PWM, LED1.C
  N7: Circuit.D7, LED2.C
  N8: Circuit.5V, S1.Pin_3, S1.Pin_4, S2.Pin_3, S2.Pin_4, Potentiometer.S, Touch_Sensor_(Linear_Pot).S
  N9: LED1.A, R1.Pin_1
  N10: LED2.A, R2.Pin_1
